// Digital circuit add_sub.dig as structural Verilog
module add_sub (
  input  [31:0] B,
  input  [31:0] A,
  input  Sub,
  output [31:0] Sum,
  output Negative,
  output Overflow
);

  wire and_1_out, and_2_out, B31, not_1_out, not_2_out, not_3_out;
  wire [31:0] add_1_s, add_2_s, add_3_s, xor_1_out;

  Add #(.Bits(32)) add_1 (.a(A), .b(B), .c_i(1'b0), .s(add_1_s));  // open: c_o
  assign xor_1_out = B ^ {32{1'b1}};  // XOr xor_1, 32 bits wide
  Add #(.Bits(32)) add_2 (.a(A), .b(xor_1_out), .c_i(1'b0), .s(add_2_s));  // open: c_o
  xor xor_2 (B31, Sub, B[31]);
  Add #(.Bits(32)) add_3 (.a(add_2_s), .b(32'h1), .c_i(1'b0), .s(add_3_s));  // open: c_o
  Multiplexer #(.Bits(32)) multiplexer_1 (.sel(Sub), .in_0(add_1_s), .in_1(add_3_s), .out({Negative, Sum[30:0]}));
  not not_1 (not_1_out, A[31]);
  not not_2 (not_2_out, B31);
  not not_3 (not_3_out, Negative);
  and and_1 (and_1_out, not_1_out, not_2_out, Negative);
  and and_2 (and_2_out, A[31], B31, not_3_out);
  or or_1 (Overflow, and_1_out, and_2_out);

  assign Sum[31] = Negative;

  // Other names for the same wires on the sheet: N = Negative
endmodule

/* Test case Add/Sub Test:
A B Sub Sum Negative Overflow
# Add
0x289322c4 0x01846399 0 0x2a17865d 0 0
0x4152a22d 0x22042121 0 0x6356c34e 0 0
0x84893212 0x0994ad1a 0 0x8e1ddf2c 1 0
0x90a8826c 0x112109fb 0 0xa1c98c67 1 0
0x5210c12d 0x3d04abbc 0 0x8f156ce9 1 1
0x90d194b5 0xb005500e 0 0x40d6e4c3 0 1

# Subtract
0x39332544 0x0435fcad 1 0x34fd2897 0 0
0x59286ab1 0x221fb76c 1 0x3708b345 0 0
0xecd55935 0x248c5a4b 1 0xc848feea 1 0
0x902a9525 0xe5454d48 1 0xaae547dd 1 0
0x8211036a 0x7b13890a 1 0x06fd7a60 0 1
0x5fe15dbe 0x8934b9b1 1 0xd6aca40d 1 1
*/
