// Digital circuit alu.dig as structural Verilog
module alu (
  input  [31:0] A,
  input  [31:0] B,
  input  Sub,
  input  [1:0] Bool,
  input  Shft,
  input  Math,
  output Z,
  output [31:0] Result
);

  wire [31:0] add_sub_1_sum, boolean_1_c, multiplexer_2_out, shifter_1_c;

  add_sub add_sub_1 (.B(B), .A(A), .Sub(Sub), .Sum(add_sub_1_sum));  // open: Negative, Overflow
  shifter shifter_1 (.A(A), .B(B), .Bool(Bool), .C(shifter_1_c));
  Multiplexer #(.Bits(32)) multiplexer_1 (.sel(Math), .in_0(multiplexer_2_out), .in_1(add_sub_1_sum), .out(Result));
  Multiplexer #(.Bits(32)) multiplexer_2 (.sel(Shft), .in_0(boolean_1_c), .in_1(shifter_1_c), .out(multiplexer_2_out));
  boolean boolean_1 (.A(A), .B(B), .Bool(Bool), .C(boolean_1_c));
  nor nor_1 (Z, Result[0], Result[1], Result[2], Result[3], Result[4], Result[5], Result[6], Result[7], Result[8], Result[9], Result[10], Result[11], Result[12], Result[13], Result[14], Result[15], Result[17], Result[18], Result[19], Result[20], Result[21], Result[22], Result[23], Result[24], Result[25], Result[26], Result[27], Result[28], Result[29], Result[30], Result[31], Result[16]);

  // Other names for the same wires on the sheet: _16 = Result[16]

  // Notes on the sheet:
  //   Control bits
  //   Inputs
  //   Outputs
endmodule

/* Test case ALU Test:
A B Sub Bool Shft Math Result Z

# Add
0x289322c4 0x01846399 0 x x 1 0x2a17865d 0
0x4152a22d 0x22042121 0 x x 1 0x6356c34e 0
0x84893212 0x0994ad1a 0 x x 1 0x8e1ddf2c 0
0x90a8826c 0x112109fb 0 x x 1 0xa1c98c67 0
0x5210c12d 0x3d04abbc 0 x x 1 0x8f156ce9 0
0x90d194b5 0xb005500e 0 x x 1 0x40d6e4c3 0

# Subtract
0x39332544 0x0435fcad 1 x x 1 0x34fd2897 0
0x59286ab1 0x221fb76c 1 x x 1 0x3708b345 0
0xecd55935 0x248c5a4b 1 x x 1 0xc848feea 0
0x902a9525 0xe5454d48 1 x x 1 0xaae547dd 0
0x8211036a 0x7b13890a 1 x x 1 0x06fd7a60 0
0x5fe15dbe 0x8934b9b1 1 x x 1 0xd6aca40d 0

# sll
0 0xdeadbeef x 0 1 0 0xdeadbeef 0
8 0xdeadbeef x 0 1 0 0xadbeef00 0
16 0xdeadbeef x 0 1 0 0xbeef0000 0
24 0xdeadbeef x 0 1 0 0xef000000 0
32 0xdeadbeef x 0 1 0 0 1
33 0xdeadbeef x 0 1 0 0 1
0xffffffff 0xdeadbeef x 0 1 0 0 1

# srl
0 0xdeadbeef x 2 1 0 0xdeadbeef 0
8 0xdeadbeef x 2 1 0 0xdeadbe 0
16 0xdeadbeef x 2 1 0 0xdead 0
24 0xdeadbeef x 2 1 0 0xde 0
32 0xdeadbeef x 2 1 0 0 1
33 0xdeadbeef x 2 1 0 0 1
0xffffffff 0xdeadbeef x 2 1 0 0 1

# sra (MSB 1)
0 0xdeadbeef x 3 1 0 0xdeadbeef 0
8 0xdeadbeef x 3 1 0 0xffdeadbe 0
16 0xdeadbeef x 3 1 0 0xffffdead 0
24 0xdeadbeef x 3 1 0 0xffffffde 0
32 0xdeadbeef x 3 1 0 0xffffffff 0
33 0xdeadbeef x 3 1 0 0xffffffff 0
0xffffffff 0xdeadbeef x 3 1 0 0xffffffff 0

# sra (MSB 0)
0 0x7eadbeef x 3 1 0 0x7eadbeef 0
8 0x7eadbeef x 3 1 0 0x7eadbe 0
16 0x7eadbeef x 3 1 0 0x7ead 0
24 0x7eadbeef x 3 1 0 0x7e 0
32 0x7eadbeef x 3 1 0 0 1
33 0x7eadbeef x 3 1 0 0 1
0xffffffff 0x7eadbeef x 3 1 0 0 1

# AND
0xdcd84709 0x768a5af3 x 0 0 0 0x54884201 0
0x3d2cd361 0xf53106ef x 0 0 0 0x35200261 0
0x28f56e63 0x854b7d0b x 0 0 0 0x00416c03 0

# OR
0x9201a3de 0x2d1a9f88 x 1 0 0 0xbf1bbfde 0
0xd15a7517 0xb900f275 x 1 0 0 0xf95af777 0
0xd81daa93 0x0ab5e9f7 x 1 0 0 0xdabdebf7 0

# XOR
0x0f9eda3f 0x885e0a47 x 2 0 0 0x87c0d078 0
0xca58eed8 0x514af1fa x 2 0 0 0x9b121f22 0
0xc7100004 0x3553ef1e x 2 0 0 0xf243ef1a 0

# NOR
0xd9537eed 0x133929ec x 3 0 0 0x24848012 0
0x66b776e8 0xb2aa434b x 3 0 0 0x09408814 0
0x745d1dab 0xafc46d88 x 3 0 0 0x00228254 0
*/
