// Digital circuit shifter.dig as structural Verilog
module shifter (
  input  [31:0] A,
  input  [31:0] B,
  input  [1:0] Bool,
  output [31:0] C
);

  wire comparator_1_gt;
  wire [5:0] SHAMT;
  wire [31:0] sll_2_out, sll_3_out, sll_out;

  Comparator #(.Bits(32)) comparator_1 (.a(A), .b(32'h20), .gt(comparator_1_gt));  // open: eq, lt
  BarrelShifter #(.Bits(32)) sll (.in(B), .shift(SHAMT), .out(sll_out));
  BarrelShifter #(.Bits(32), .barrelShifterMode("arithmetic"), .direction("right")) sll_2 (
    .in(B), .shift(SHAMT), .out(sll_2_out));
  BarrelShifter #(.Bits(32), .direction("right")) sll_3 (.in(B), .shift(SHAMT), .out(sll_3_out));
  Multiplexer #(.Bits(32), .Selector_Bits(2)) multiplexer_1 (
    .sel(Bool), .in_0(sll_out), .in_1({32{1'b0}}), .in_2(sll_3_out), .in_3(sll_2_out), .out(C));
  Multiplexer #(.Bits(6)) multiplexer_2 (.sel(comparator_1_gt), .in_0(A[5:0]), .in_1(6'b100000), .out(SHAMT));
endmodule

/* Test case Bidirectional Shifter Test:
A B Bool C
# sll
0 0xdeadbeef 0 0xdeadbeef
8 0xdeadbeef 0 0xadbeef00
16 0xdeadbeef 0 0xbeef0000
24 0xdeadbeef 0 0xef000000
32 0xdeadbeef 0 0
33 0xdeadbeef 0 0
0xffffffff 0xdeadbeef 0 0

# srl
0 0xdeadbeef 2 0xdeadbeef
8 0xdeadbeef 2 0xdeadbe
16 0xdeadbeef 2 0xdead
24 0xdeadbeef 2 0xde
32 0xdeadbeef 2 0
33 0xdeadbeef 2 0
0xffffffff 0xdeadbeef 0 0

# sra (MSB 1)
0 0xdeadbeef 3 0xdeadbeef
8 0xdeadbeef 3 0xffdeadbe
16 0xdeadbeef 3 0xffffdead
24 0xdeadbeef 3 0xffffffde
32 0xdeadbeef 3 0xffffffff
33 0xdeadbeef 3 0xffffffff
0xffffffff 0xdeadbeef 3 0xffffffff

# sra (MSB 0)
0 0x7eadbeef 3 0x7eadbeef
8 0x7eadbeef 3 0x7eadbe
16 0x7eadbeef 3 0x7ead
24 0x7eadbeef 3 0x7e
32 0x7eadbeef 3 0
33 0x7eadbeef 3 0
0xffffffff 0x7eadbeef 3 0
*/
