// Digital circuit counter.dig as structural Verilog
module counter (
  input  Up,
  input  CLK,
  output Q_2,
  output Q_1,
  output Q_0
);

  wire T1, T2;

  and and_1 (T1, Up, Q_0);
  and and_2 (T2, Up, Q_1, Q_0);
  T_FF t_ff_1 (.T(T2), .C(CLK), .Q(Q_2));  // open: nQ
  T_FF t_ff_2 (.T(T1), .C(CLK), .Q(Q_1));  // open: nQ
  T_FF t_ff_3 (.T(Up), .C(CLK), .Q(Q_0));  // open: nQ

  // Other names for the same wires on the sheet: Q0 = Q_0; Q1 = Q_1; T0 = Up

  // Notes on the sheet:
  //   CLK: Hz: 1000
endmodule

/* Test case:
Up CLK Q_2 Q_1 Q_0
loop(A, 32)
	bits(2,A) bits(3,(A+1)/4)
end loop
*/
