// Digital circuit enabled_d_flip_flop.dig as structural Verilog
module enabled_d_flip_flop (
  input  C,
  input  en,
  input  D,
  output Q
);

  wire and_1_out;

  and and_1 (and_1_out, C, en);
  D_FF_AS d_ff_as_1 (.Set(1'b0), .D(D), .C(and_1_out), .Clr(1'b0), .Q(Q));  // open: nQ
endmodule

/* Test case:
C D en Q
0 0 0 0
C 0 0 0
C 0 1 0
C 1 0 0
C 1 1 1
C 0 0 1
C 1 0 1
C 0 1 0
*/
