// Digital circuit enabled_register.dig as structural Verilog
module enabled_register (
  input  CLK,
  input  [3:0] D,
  input  en,
  output [3:0] Q
);

  enabled_d_flip_flop enabled_d_flip_flop_1 (.C(CLK), .en(en), .D(D[0]), .Q(Q[0]));
  enabled_d_flip_flop enabled_d_flip_flop_2 (.C(CLK), .en(en), .D(D[1]), .Q(Q[1]));
  enabled_d_flip_flop enabled_d_flip_flop_3 (.C(CLK), .en(en), .D(D[2]), .Q(Q[2]));
  enabled_d_flip_flop enabled_d_flip_flop_4 (.C(CLK), .en(en), .D(D[3]), .Q(Q[3]));
endmodule

/* Test case:
CLK D en Q
0 0 0 0
C 0 0 0
C 7 0 0

# enable 1 and write 0-15
loop(n, 16)
	C (n) 1 (n)
end loop

# enable 0, D is 0-15 but should not be written
loop(n, 16)
	C (n) 0 15
end loop

C 0 1 0
*/
