// Digital circuit example_register.dig as structural Verilog
module example_register (
  input  CLK,
  input  en,
  input  [3:0] D,
  output [3:0] Q
);

  Register #(.Bits(4)) register_1 (.D(D), .C(CLK), .en(en), .Q(Q));
endmodule

/* Test case:
CLK D en Q
0 0 0 0
C 0 0 0
C 7 0 0

# enable 1 and write 0-15
loop(n, 16)
	C (n) 1 (n)
end loop

# enable 0, D is 0-15 but should not be written
loop(n, 16)
	C (n) 0 15
end loop

C 0 1 0
*/
