// Digital circuit seven_seg.dig as structural Verilog
module seven_seg (
  input  A,
  input  CLK,
  output F_a,
  output F_g,
  output F_b,
  output F_c,
  output F_d,
  output F_e,
  output F_f
);

  wire A_t, and_1_out, and_2_out, and_3_out, and_4_out, and_5_out, and_6_out, and_7_out, and_8_out,
       and_9_out, and_10_out, and_11_out, and_12_out, and_13_out, and_14_out, and_15_out, and_16_out,
       and_17_out, and_18_out, and_19_out, and_20_out, and_21_out, and_22_out, and_23_out, and_24_out,
       and_25_out, and_26_out, and_27_out, and_28_out, and_29_out, and_30_out, and_31_out, and_32_out,
       and_33_out, B, B_t, C, C_t, D, D_t;

  and and_1 (and_1_out, B_t, D_t);
  and and_2 (and_2_out, B, C);
  and and_3 (and_3_out, A_t, C);
  and and_4 (and_4_out, A_t, B, D);
  and and_5 (and_5_out, A, B_t, C_t);
  counter counter_1 (.Up(1'b1), .CLK(CLK), .Q_2(B), .Q_1(C), .Q_0(D));
  or or_1 (F_a, and_1_out, and_2_out, and_3_out, and_4_out, and_5_out);
  not not_1 (A_t, A);
  not not_2 (B_t, B);
  not not_3 (C_t, C);
  not not_4 (D_t, D);
  and and_6 (and_6_out, B_t, D_t);
  and and_7 (and_7_out, B_t, C_t);
  and and_8 (and_8_out, A_t, C, D);
  and and_9 (and_9_out, A, C_t, D);
  and and_10 (and_10_out, A_t, C_t, D_t);
  or or_2 (F_b, and_6_out, and_7_out, and_8_out, and_9_out, and_10_out);
  and and_11 (and_11_out, A, B_t);
  and and_12 (and_12_out, C_t, D);
  and and_13 (and_13_out, A_t, B);
  and and_14 (and_14_out, A_t, D);
  and and_15 (and_15_out, B_t, C_t);
  or or_3 (F_c, and_11_out, and_12_out, and_13_out, and_14_out, and_15_out);
  and and_16 (and_16_out, A, B, D_t);
  and and_17 (and_17_out, B_t, C_t, D_t);
  and and_18 (and_18_out, B, C_t, D);
  and and_19 (and_19_out, A_t, C, D_t);
  and and_20 (and_20_out, A, B_t, D);
  and and_21 (and_21_out, A_t, B_t, C);
  or or_4 (F_d, and_16_out, and_17_out, and_18_out, and_19_out, and_20_out, and_21_out);
  and and_22 (and_22_out, B_t, D_t);
  and and_23 (and_23_out, C, D_t);
  and and_24 (and_24_out, A, B);
  and and_25 (and_25_out, A, C);
  Seven_Seg seven_seg_1 (.a(F_a), .b(F_b), .c(F_c), .d(F_d), .e(F_e), .f(F_f), .g(F_g), .dp(1'b0));
  or or_5 (F_e, and_22_out, and_23_out, and_24_out, and_25_out);
  and and_26 (and_26_out, A, B_t);
  and and_27 (and_27_out, A, C);
  and and_28 (and_28_out, B, C, D_t);
  and and_29 (and_29_out, A_t, B, C_t);
  and and_30 (and_30_out, A_t, C_t, D_t);
  or or_6 (F_f, and_26_out, and_27_out, and_28_out, and_29_out, and_30_out);
  and and_31 (and_31_out, B_t, C);
  and and_32 (and_32_out, B, D_t);
  and and_33 (and_33_out, B, C_t);
  or or_7 (F_g, A, and_31_out, and_32_out, and_33_out);

  // Notes on the sheet:
  //   CLK: Hz: 2
endmodule

/* Test case:
CLK A F_a F_b F_c F_d F_e F_f F_g
# 0-7
0 0 1 1 1 1 1 1 0
C 0 0 1 1 0 0 0 0
C 0 1 1 0 1 1 0 1
C 0 1 1 1 1 0 0 1
C 0 0 1 1 0 0 1 1
C 0 1 0 1 1 0 1 1
C 0 1 0 1 1 1 1 1
C 0 1 1 1 0 0 0 0
C 0 1 1 1 1 1 1 0

# 8-f
0 1 1 1 1 1 1 1 1
C 1 1 1 1 1 0 1 1
C 1 1 1 1 0 1 1 1
C 1 0 0 1 1 1 1 1
C 1 0 0 0 1 1 0 1
C 1 0 1 1 1 1 0 1
C 1 1 0 0 1 1 1 1
C 1 1 0 0 0 1 1 1
C 1 1 1 1 1 1 1 1
*/
