// Digital circuit alu.dig as structural Verilog
module alu (
  input  [31:0] A,
  input  [31:0] B,
  input  [4:0] ALUFN,
  output Z,
  output [31:0] Result
);

  wire C, Negative, Overflow;
  wire [0:0] A_lt_B;
  wire [31:0] C_boolean, C_shift, multiplexer_1_out, multiplexer_3_out, Sum;

  add_sub add_sub_1 (.B(B), .A(A), .Sub(ALUFN[4]), .Sum(Sum), .Negative(Negative), .Overflow(Overflow), .C(C));
  comparator comparator_1 (.Negative(Negative), .Overflow(Overflow), .C(C), .Bool_0(ALUFN[2]), .A_lt_B(A_lt_B[0]));
  shifter shifter_1 (.A(A), .B(B), .Bool(ALUFN[3:2]), .C(C_shift));
  Multiplexer #(.Bits(32)) multiplexer_1 (
    .sel(ALUFN[1]), .in_0(Sum), .in_1({{31{1'b0}}, A_lt_B[0]}), .out(multiplexer_1_out));
  Multiplexer #(.Bits(32)) multiplexer_2 (
    .sel(ALUFN[0]), .in_0(multiplexer_3_out), .in_1(multiplexer_1_out), .out(Result));
  Multiplexer #(.Bits(32)) multiplexer_3 (.sel(ALUFN[1]), .in_0(C_boolean), .in_1(C_shift), .out(multiplexer_3_out));
  boolean boolean_1 (.A(A), .B(B), .Bool(ALUFN[3:2]), .C(C_boolean));
  nor nor_1 (Z, Result[0], Result[1], Result[2], Result[3], Result[4], Result[5], Result[6], Result[7], Result[8], Result[9], Result[10], Result[11], Result[12], Result[13], Result[14], Result[15], Result[17], Result[18], Result[19], Result[20], Result[21], Result[22], Result[23], Result[24], Result[25], Result[26], Result[27], Result[28], Result[29], Result[30], Result[31], Result[16]);

  // Other names for the same wires on the sheet: Math = ALUFN[0]; Shft = ALUFN[1]; Bool[1:0] = ALUFN[3:2];
  //   Bool_0 = ALUFN[2]; Sub = ALUFN[4]; _16 = Result[16]

  // Notes on the sheet:
  //   ALUFN: Sub Bool_1 Bool_0 Shft Math
  //   Control bits
  //   Inputs
  //   Outputs
endmodule

/* Test case ALU Test:
A B ALUFN Result Z

# Add (0xx01)
loop(bool, 4)
	let alufn = bool << 2 | 1;
	0x289322c4 0x01846399 (alufn) 0x2a17865d 0
	0x4152a22d 0x22042121 (alufn) 0x6356c34e 0
	0x84893212 0x0994ad1a (alufn) 0x8e1ddf2c 0
	0x90a8826c 0x112109fb (alufn) 0xa1c98c67 0
	0x5210c12d 0x3d04abbc (alufn) 0x8f156ce9 0
	0x90d194b5 0xb005500e (alufn) 0x40d6e4c3 0
end loop

# Subtract (1xx01)
loop(bool, 4)
	let alufn = 1 << 4 | bool << 2 | 1;
	0x39332544 0x0435fcad (alufn) 0x34fd2897 0
	0x59286ab1 0x221fb76c (alufn) 0x3708b345 0
	0xecd55935 0x248c5a4b (alufn) 0xc848feea 0
	0x902a9525 0xe5454d48 (alufn) 0xaae547dd 0
	0x8211036a 0x7b13890a (alufn) 0x06fd7a60 0
	0x5fe15dbe 0x8934b9b1 (alufn) 0xd6aca40d 0
end loop

# LT (1x011)
loop(bool1, 2)
	let alufn = 1 << 4 | bool1 << 3 | 0b11;
	0 0 (alufn) 0 1
	0xFFFFFFFF 0 (alufn) 1 0
	0 1 (alufn) 1 0
	0x289322c4 0x01846399 (alufn) 0 1
	0x4152a22d 0x22042121 (alufn) 0 1
	0x84893212 0x0994ad1a (alufn) 1 0
	0x90a8826c 0x112109fb (alufn) 1 0
	0x5210c12d 0x3d04abbc (alufn) 0 1
	0x90d194b5 0xb005500e (alufn) 1 0
	0x39332544 0x0435fcad (alufn) 0 1
	0x59286ab1 0x221fb76c (alufn) 0 1
	0xecd55935 0x248c5a4b (alufn) 1 0
	0x902a9525 0xe5454d48 (alufn) 1 0
	0x8211036a 0x7b13890a (alufn) 1 0
	0x5fe15dbe 0x8934b9b1 (alufn) 0 1
end loop

# LTU (1x111)
loop(bool1, 2)
	let alufn = 1 << 4 | bool1 << 3 | 0b111;
	0 0 (alufn) 0 1
	0xFFFFFFFF 0 (alufn) 0 1
	0 1 (alufn) 1 0
	0x289322c4 0x01846399 (alufn) 0 1
	0x4152a22d 0x22042121 (alufn) 0 1
	0x84893212 0x0994ad1a (alufn) 0 1
	0x90a8826c 0x112109fb (alufn) 0 1
	0x5210c12d 0x3d04abbc (alufn) 0 1
	0x90d194b5 0xb005500e (alufn) 1 0
	0x39332544 0x0435fcad (alufn) 0 1
	0x59286ab1 0x221fb76c (alufn) 0 1
	0xecd55935 0x248c5a4b (alufn) 0 1
	0x902a9525 0xe5454d48 (alufn) 1 0
	0x8211036a 0x7b13890a (alufn) 0 1
	0x5fe15dbe 0x8934b9b1 (alufn) 1 0
end loop

# SLL (x0010)
loop(sub, 2)
	let alufn = sub << 4 | 0b10;
	0 0xdeadbeef (alufn) 0xdeadbeef 0
	8 0xdeadbeef (alufn) 0xadbeef00 0
	16 0xdeadbeef (alufn) 0xbeef0000 0
	24 0xdeadbeef (alufn) 0xef000000 0
	32 0xdeadbeef (alufn) 0 1
	33 0xdeadbeef (alufn) 0 1
	0xffffffff 0xdeadbeef (alufn) 0 1
end loop

# SRL (x1010)
loop(sub, 2)
	let alufn = sub << 4 | 0b1010;
	0 0xdeadbeef (alufn) 0xdeadbeef 0
	8 0xdeadbeef (alufn) 0xdeadbe 0
	16 0xdeadbeef (alufn) 0xdead 0
	24 0xdeadbeef (alufn) 0xde 0
	32 0xdeadbeef (alufn) 0 1
	33 0xdeadbeef (alufn) 0 1
	0xffffffff 0xdeadbeef (alufn) 0 1
end loop

# SRA (x1110)
loop(sub, 2)
	let alufn = sub << 4 | 0b1110;

	# MSB 1
	0 0xdeadbeef (alufn) 0xdeadbeef 0
	8 0xdeadbeef (alufn) 0xffdeadbe 0
	16 0xdeadbeef (alufn) 0xffffdead 0
	24 0xdeadbeef (alufn) 0xffffffde 0
	32 0xdeadbeef (alufn) 0xffffffff 0
	33 0xdeadbeef (alufn) 0xffffffff 0
	0xffffffff 0xdeadbeef (alufn) 0xffffffff 0

	# MSB 0
	0 0x7eadbeef (alufn) 0x7eadbeef 0
	8 0x7eadbeef (alufn) 0x7eadbe 0
	16 0x7eadbeef (alufn) 0x7ead 0
	24 0x7eadbeef (alufn) 0x7e 0
	32 0x7eadbeef (alufn) 0 1
	33 0x7eadbeef (alufn) 0 1
	0xffffffff 0x7eadbeef (alufn) 0 1
end loop

# AND (x0000)
loop(sub, 2)
	let alufn = sub << 4;
	0xdcd84709 0x768a5af3 (alufn) 0x54884201 0
	0x3d2cd361 0xf53106ef (alufn) 0x35200261 0
	0x28f56e63 0x854b7d0b (alufn) 0x00416c03 0
end loop

# OR (x0100)
loop(sub, 2)
	let alufn = sub << 4 | 0b100;
	0x9201a3de 0x2d1a9f88 (alufn) 0xbf1bbfde 0
	0xd15a7517 0xb900f275 (alufn) 0xf95af777 0
	0xd81daa93 0x0ab5e9f7 (alufn) 0xdabdebf7 0
end loop

# XOR (x1000)
loop(sub, 2)
	let alufn = sub << 4 | 0b1000;
	0x0f9eda3f 0x885e0a47 (alufn) 0x87c0d078 0
	0xca58eed8 0x514af1fa (alufn) 0x9b121f22 0
	0xc7100004 0x3553ef1e (alufn) 0xf243ef1a 0
end loop

# NOR (x1100)
loop(sub, 2)
	let alufn = sub << 4 | 0b1100;
	0xd9537eed 0x133929ec (alufn) 0x24848012 0
	0x66b776e8 0xb2aa434b (alufn) 0x09408814 0
	0x745d1dab 0xafc46d88 (alufn) 0x00228254 0
end loop
*/
