// Digital circuit control_unit.dig as structural Verilog
module control_unit (
  input  [5:0] opcode,
  input  [5:0] funct,
  input  Z,
  output WERF,
  output [1:0] WDSEL,
  output [1:0] WASEL,
  output [1:0] ASEL,
  output BSEL,
  output SgnExt,
  output Wr,
  output [4:0] ALUFN,
  output [1:0] PCSEL
);

  wire _0, _1, _2, _3, _4, _5, _6, _7, _8, _9, _10, _11, _12, _13, _14, _15, _16, _17, _18, _19, aaa, beq,
       bne, comparator_1_eq, comparator_2_eq, comparator_3_eq, comparator_4_eq, comparator_5_eq,
       comparator_6_eq, comparator_7_eq, comparator_8_eq, comparator_9_eq, comparator_10_eq,
       comparator_11_eq, comparator_12_eq, comparator_13_eq, comparator_14_eq, comparator_15_eq,
       comparator_16_eq, not_1_out;
  wire [1:0] multiplexer_1_out;
  wire [4:0] InstructionIndex;

  Comparator #(.Bits(6)) comparator_1 (.a(opcode), .b({6{1'b0}}), .eq(comparator_1_eq));  // open: gt, lt
  Comparator #(.Bits(6)) comparator_2 (.a(funct), .b(6'b100000), .eq(comparator_2_eq));  // open: gt, lt
  Comparator #(.Bits(6)) comparator_3 (.a(opcode), .b({6{1'b0}}), .eq(comparator_3_eq));  // open: gt, lt
  Comparator #(.Bits(6)) comparator_4 (.a(funct), .b(6'b100010), .eq(comparator_4_eq));  // open: gt, lt
  Comparator #(.Bits(6)) comparator_5 (.a(opcode), .b({6{1'b0}}), .eq(comparator_5_eq));  // open: gt, lt
  Comparator #(.Bits(6)) comparator_6 (.a(funct), .b(6'b100100), .eq(comparator_6_eq));  // open: gt, lt
  Comparator #(.Bits(6)) comparator_7 (.a(opcode), .b({6{1'b0}}), .eq(comparator_7_eq));  // open: gt, lt
  Comparator #(.Bits(6)) comparator_8 (.a(funct), .b(6'b100101), .eq(comparator_8_eq));  // open: gt, lt
  Comparator #(.Bits(6)) comparator_9 (.a(opcode), .b({6{1'b0}}), .eq(comparator_9_eq));  // open: gt, lt
  Comparator #(.Bits(6)) comparator_10 (.a(funct), .b(6'b100110), .eq(comparator_10_eq));  // open: gt, lt
  Comparator #(.Bits(6)) comparator_11 (.a(opcode), .b({6{1'b0}}), .eq(comparator_11_eq));  // open: gt, lt
  Comparator #(.Bits(6)) comparator_12 (.a(funct), .b(6'b100111), .eq(comparator_12_eq));  // open: gt, lt
  Comparator #(.Bits(6)) comparator_13 (.a(opcode), .b({6{1'b0}}), .eq(comparator_13_eq));  // open: gt, lt
  Comparator #(.Bits(6)) comparator_14 (.a(funct), .b(6'b101010), .eq(comparator_14_eq));  // open: gt, lt
  Comparator #(.Bits(6)) comparator_15 (.a(opcode), .b({6{1'b0}}), .eq(comparator_15_eq));  // open: gt, lt
  Comparator #(.Bits(6)) comparator_16 (.a(funct), .b(6'b101011), .eq(comparator_16_eq));  // open: gt, lt
  and and_1 (_0, comparator_1_eq, comparator_2_eq);
  and and_2 (_1, comparator_3_eq, comparator_4_eq);
  and and_3 (_2, comparator_5_eq, comparator_6_eq);
  and and_4 (_3, comparator_7_eq, comparator_8_eq);
  and and_5 (_4, comparator_9_eq, comparator_10_eq);
  and and_6 (_5, comparator_11_eq, comparator_12_eq);
  and and_7 (_6, comparator_13_eq, comparator_14_eq);
  and and_8 (_7, comparator_15_eq, comparator_16_eq);
  Comparator #(.Bits(6)) comparator_17 (.a(opcode), .b(6'b000010), .eq(_8));  // open: gt, lt
  Comparator #(.Bits(6)) comparator_18 (.a(opcode), .b(6'b000100), .eq(_9));  // open: gt, lt
  Comparator #(.Bits(6)) comparator_19 (.a(opcode), .b(6'b000101), .eq(_10));  // open: gt, lt
  Comparator #(.Bits(6)) comparator_20 (.a(opcode), .b(6'b001000), .eq(_11));  // open: gt, lt
  Comparator #(.Bits(6)) comparator_21 (.a(opcode), .b(6'b001001), .eq(_12));  // open: gt, lt
  Comparator #(.Bits(6)) comparator_22 (.a(opcode), .b(6'b001010), .eq(_13));  // open: gt, lt
  Comparator #(.Bits(6)) comparator_23 (.a(opcode), .b(6'b001011), .eq(_14));  // open: gt, lt
  Comparator #(.Bits(6)) comparator_24 (.a(opcode), .b(6'b001100), .eq(_15));  // open: gt, lt
  Comparator #(.Bits(6)) comparator_25 (.a(opcode), .b(6'b001101), .eq(_16));  // open: gt, lt
  Comparator #(.Bits(6)) comparator_26 (.a(opcode), .b(6'b001110), .eq(_17));  // open: gt, lt
  Comparator #(.Bits(6)) comparator_27 (.a(opcode), .b(6'b100011), .eq(_18));  // open: gt, lt
  Comparator #(.Bits(6)) comparator_28 (.a(opcode), .b(6'b101011), .eq(_19));  // open: gt, lt
  not not_1 (not_1_out, Z);
  and and_9 (beq, _9, Z);
  and and_10 (bne, _10, not_1_out);
  or or_1 (aaa, beq, bne);
  PriorityEncoder #(.Selector_Bits(5)) priorityencoder_1 (
    .in0(_0), .in1(_1), .in2(_2), .in3(_3), .in4(_4), .in5(_5), .in6(_6), .in7(_7), .in8(_8), .in9(_9),
    .in10(_10), .in11(_11), .in12(_12), .in13(_13), .in14(_14), .in15(_15), .in16(_16), .in17(_17),
    .in18(_18), .in19(_19), .in20(1'b0), .in21(1'b0), .in22(1'b0), .in23(1'b0), .in24(1'b0), .in25(1'b0),
    .in26(1'b0), .in27(1'b0), .in28(1'b0), .in29(1'b0), .in30(1'b0), .in31(1'b0), .num(InstructionIndex));  // open: any
  ROM #(.AddrBits(5), .Bits(15)) Controls (
    .A(InstructionIndex), .sel(1'b1), .D({WERF, WDSEL, WASEL, ASEL, BSEL, SgnExt, Wr, ALUFN}));
  Multiplexer #(.Bits(2)) multiplexer_1 (.sel(aaa), .in_0(2'b00), .in_1(2'b01), .out(multiplexer_1_out));
  Multiplexer #(.Bits(2)) multiplexer_2 (.sel(_8), .in_0(multiplexer_1_out), .in_1(2'b10), .out(PCSEL));

  // Other names for the same wires on the sheet: opcode_0 = opcode[0]; opcode_1 = opcode[1]; opcode_2 = opcode[2];
  //   opcode_3 = opcode[3]; opcode_4 = opcode[4]; opcode_5 = opcode[5]

  // Notes on the sheet:
  //   contents of Controls (hex, n*v repeats v):
  //   5001,5011,5000,5004,5008,500c,5013,5017,0,51,51,54c1,54c1,54d3
  //   ,54d7,5480,5484,5488,64c1,e1
endmodule

/* Test case add:
opcode funct Z WERF WDSEL WASEL ASEL BSEL SgnExt Wr ALUFN PCSEL
0 32 x 1 1 0 0 0 0 0 1 0
*/
