// Digital circuit cpu.dig as structural Verilog
module cpu (
  input  CLK,
  output [31:0] RD1,
  output [31:0] RD2,
  output [31:0] PC
);

  wire SeB, SgnExt, WERF, Wr, Z;
  wire [1:0] PCSEL, SeA, WASEL, WDSEL;
  wire [3:0] _3128;
  wire [4:0] ALUFN, WA;
  wire [5:0] funct;
  wire [27:6] Instr;
  wire [31:0] AddO, ALUO, Imm32, OutA, OutB, OutC, PC_plus_4, ShiO, WD, WD1;

  Multiplexer #(.Selector_Bits(2), .Bits(32)) multiplexer_1 (
    .sel(SeA), .in_0(RD1), .in_1({{27{1'b0}}, Instr[10:6]}), .in_2(32'h10), .in_3({32{1'b0}}), .out(OutA));
  Add #(.Bits(32)) add_1 (.a(PC_plus_4), .b(ShiO), .c_i(1'b0), .s(AddO));  // open: c_o
  BarrelShifter #(.Bits(32)) barrelshifter_1 (.in(Imm32), .shift(6'b000010), .out(ShiO));
  Multiplexer #(.Selector_Bits(2), .Bits(32)) multiplexer_2 (
    .sel(PCSEL), .in_0(PC_plus_4), .in_1(AddO), .in_2({_3128, Instr[25:6], funct, 2'b00}), .in_3(RD1),
    .out(OutC));
  Multiplexer #(.Selector_Bits(2), .Bits(32)) multiplexer_3 (
    .sel(WDSEL), .in_0(PC_plus_4), .in_1(ALUO), .in_2(WD1), .in_3({32{1'b0}}), .out(WD));
  control_unit control_unit_1 (
    .opcode({_3128, Instr[27:26]}), .funct(funct), .Z(Z), .WERF(WERF), .WDSEL(WDSEL), .WASEL(WASEL),
    .ASEL(SeA), .BSEL(SeB), .SgnExt(SgnExt), .Wr(Wr), .ALUFN(ALUFN), .PCSEL(PCSEL));
  Register #(.Bits(32)) u_PC (.D(OutC), .C(CLK), .en(1'b1), .Q(PC));
  BitExtender #(.inputBits(16), .outputBits(32)) bitextender_1 (.in({Instr[15:6], funct}), .out(Imm32));
  Add #(.Bits(32)) add_2 (.a(PC), .b(32'h4), .c_i(1'b0), .s(PC_plus_4));  // open: c_o
  Multiplexer #(.Selector_Bits(2), .Bits(5)) multiplexer_4 (
    .sel(WASEL), .in_0(Instr[15:11]), .in_1(Instr[20:16]), .in_2({5{1'b1}}), .in_3(5'b11011), .out(WA));
  Multiplexer #(.Bits(32)) multiplexer_5 (.sel(SeB), .in_0(RD2), .in_1(Imm32), .out(OutB));
  ROM #(.AddrBits(10), .isProgramMemory("true"), .Bits(32)) Instruction_Memory (
    .A(PC[9:0]), .sel(1'b1), .D({_3128, Instr, funct}));
  alu alu_1 (.A(OutA), .B(OutB), .ALUFN(ALUFN), .Z(Z), .Result(ALUO));
  register_file register_file_1 (
    .WA(WA), .WE(WERF), .WD(WD), .CLK(CLK), .RA1(Instr[25:21]), .RA2(Instr[20:16]), .RD1(RD1), .RD2(RD2));
  RAMDualPort #(.AddrBits(12), .Bits(32)) Data_Memory (
    .A(ALUO[11:0]), .Din(RD2), .str(Wr), .C(CLK), .ld(1'b1), .D(WD1));

  // Other names for the same wires on the sheet: Instr (some bits) = {_3128, funct}; J[25:0] = {Instr[25:6], funct};
  //   M[31:2] = {_3128, Instr[25:6], funct}; mm[15:0] = {Instr[15:6], funct}; shamt[4:0] = Instr[10:6];
  //   Rd[4:0] = Instr[15:11]; Rt[4:0] = Instr[20:16]; Rs[4:0] = Instr[25:21]; opcode[5:0] = {_3128, Instr[27:26]};
  //   PC_9_0[9:0] = PC[9:0]; PC_31_28[3:0] = PC[31:28]
endmodule

/* Test case addi:
CLK PC RD1 RD2
program(0x2004ffec, 0, 0, 0, 0x20857fff, 0, 0, 0, 0x20a67018, 0, 0, 0, 0x20c75311, 0, 0, 0, 0x20800000, 0, 0, 0, 0x20000000, 0, 0, 0, 0x20088000, 0, 0, 0, 0x21000000)
0 0 0 0		# addi $4, $0, -20
C 4 (-20) 0	# addi $5, $4, 0x7FFF
C 8 32747 0	# addi $6, $5, 0x7018
C 12 61443 0	# addi $7, $6, 0x5311
C 16 (-20) 0	# addi $0, $4, 0
C 20 0 0	# addi $0, $0, 0
C 24 0 0	# addi $8, $0, -0x8000	# the immediate field is 0x8000, and $8 is 0xffff8000 (sign-extended)
C 28 0xffff8000 0	# addi $0, $8, 0
*/

/* Test case or:
CLK PC RD1 RD2
program(0x2008000c, 0, 0, 0, 0x2009000a, 0, 0, 0, 0x01095025, 0, 0, 0, 0x21400000)
0 0 0 0		# addi $8, $0, 12
C 4 0 0		# addi $9, $0, 10
C 8 12 10	# or $10, $8, $9
C 12 14 0	# addi $0, $10, 0
*/

/* Test case sltu:
CLK PC RD1 RD2
program(0x200f0007, 0, 0, 0, 0x2010000d, 0, 0, 0, 0x2011fffd, 0, 0, 0, 0x01f0902b, 0, 0, 0, 0x22400000, 0, 0, 0, 0x020f902b, 0, 0, 0, 0x22400000, 0, 0, 0, 0x01ef902b, 0, 0, 0, 0x22400000, 0, 0, 0, 0x022f902b, 0, 0, 0, 0x22400000, 0, 0, 0, 0x01f1902b, 0, 0, 0, 0x22400000)
0 0 0 0     # addi $15, $0, 7
C 4 0 0     # addi $16, $0, 13
C 8 0 0     # addi $17, $0, -3
C 12 7 13   # slt $18, $15, $16
C 16 1 0    # addi $0, $18, 0
C 20 13 7   # sltu $18, $16, $15
C 24 0 0    # addi $0, $18, 0
C 28 7 7    # sltu $18, $15, $15
C 32 0 0    # addi $0, $18, 0
C 36 (-3) 7 # sltu $18, $17, $15
C 40 0 0    # addi $0, $18, 0
C 44 7 (-3) # sltu $18, $15, $17
C 48 1 0    # addi $0, $18, 0
*/

/* Test case addiu:
CLK PC RD1 RD2
program(0x2404ffec, 0, 0, 0, 0x24857fff, 0, 0, 0, 0x24a67018, 0, 0, 0, 0x24c75311, 0, 0, 0, 0x24800000, 0, 0, 0, 0x24000000, 0, 0, 0, 0x24088000, 0, 0, 0, 0x25000000)
0 0 0 0		# addiu $4, $0, -20
C 4 (-20) 0	# addiu $5, $4, 0x7FFF
C 8 32747 0	# addiu $6, $5, 0x7018
C 12 61443 0	# addiu $7, $6, 0x5311
C 16 (-20) 0	# addiu $0, $4, 0
C 20 0 0	# addiu $0, $0, 0
C 24 0 0	# addiu $8, $0, -0x8000	# the immediate field is 0x8000, and $8 is 0xffff8000 (sign-extended)
C 28 0xffff8000 0	# addiu $0, $8, 0
*/

/* Test case ori:
CLK PC RD1 RD2
program(0x200b000c, 0, 0, 0, 0x356c000a, 0, 0, 0, 0x21800000)
0 0 0 0		# addi $11, $0, 12
C 4 12 0	# ori $12, $11, 10
C 8 14 0	# addi $0, $12, 0
*/

/* Test case add:
CLK PC RD1 RD2
program(0x200a0002, 0, 0, 0, 0x214b0003, 0, 0, 0, 0x014b6020, 0, 0, 0, 0x018c6820, 0, 0, 0, 0x21a00000)
0 0 0 0		# addi $10, $0, 2
C 4 2 0		# addi $11, $10, 3
C 8 2 5 	# add $12, $10, $11
C 12 7 7	# add $13, $12, $12
C 16 14 0	# addi $0, $13, 0
*/

/* Test case xor:
CLK PC RD1 RD2
program(0x2008000c, 0, 0, 0, 0x2009000a, 0, 0, 0, 0x01095026, 0, 0, 0, 0x21400000)
0 0 0 0		# addi $8, $0, 12
C 4 0 0		# addi $9, $0, 10
C 8 12 10	# xor $10, $8, $9
C 12 6 0	# addi $0, $10, 0
*/

/* Test case j:
CLK PC RD1 RD2
program(0x20140001, 0, 0, 0, 0x08000003, 0, 0, 0, 0x20140002, 0, 0, 0, 0x22800000)
0 0 0 0		# addi $20, $0, 1
C 4 x x		# j skip
C 12 1 0	# addi $0, $20, 0
*/

/* Test case slti:
CLK PC RD1 RD2
program(0x200f0007, 0, 0, 0, 0x2010fffd, 0, 0, 0, 0x29f1000d, 0, 0, 0, 0x22200000, 0, 0, 0, 0x29f10003, 0, 0, 0, 0x22200000, 0, 0, 0, 0x28110000, 0, 0, 0, 0x22200000, 0, 0, 0, 0x2a110000, 0, 0, 0, 0x22200000, 0, 0, 0, 0x2811fffd, 0, 0, 0, 0x22200000)
0 0 0 0     # addi $15, $0, 7
C 4 0 0     # addi $16, $0, -3
C 8 7 0     # slti $17, $15, 13
C 12 1 0    # addi $0, $17, 0
C 16 7 1    # slti $17, $15, 3
C 20 0 0    # addi $0, $17, 0
C 24 0 0    # slti $17, $0, 0
C 28 0 0    # addi $0, $17, 0
C 32 (-3) 0 # slti $17, $16, 0
C 36 1 0    # addi $0, $17, 0
C 40 0 1    # slti $17, $0, -3
C 44 0 0    # addi $0, $17, 0
*/

/* Test case xori:
CLK PC RD1 RD2
program(0x200b000c, 0, 0, 0, 0x396c000a, 0, 0, 0, 0x21800000)
0 0 0 0		# addi $11, $0, 12
C 4 12 0	# xori $12, $11, 10
C 8 6 0		# addi $0, $12, 0
*/

/* Test case sub:
CLK PC RD1 RD2
program(0x200a0003, 0, 0, 0, 0x200b0002, 0, 0, 0, 0x014b6022, 0, 0, 0, 0x21800000, 0, 0, 0, 0x016a6022, 0, 0, 0, 0x21800000, 0, 0, 0, 0x018c6022, 0, 0, 0, 0x21800000)
0 0 0 0		# addi $10, $0, 3
C 4 0 0		# addi $11, $0, 2
C 8 3 2		# sub $12, $10, $11
C 12 1 0	# addi $0, $12, 0
C 16 2 3	# sub $12, $11, $10
C 20 (-1) 0	# addi $0, $12, 0
C 24 (-1) (-1)	# sub $12, $12, $12
C 28 0 0	# addi $0, $12, 0
*/

/* Test case nor:
CLK PC RD1 RD2
program(0x2008000c, 0, 0, 0, 0x2009000a, 0, 0, 0, 0x01095027, 0, 0, 0, 0x21400000)
0 0 0 0		# addi $8, $0, 12
C 4 0 0		# addi $9, $0, 10
C 8 12 10	# nor $10, $8, $9
C 12 0xffffffff1 0	# addi $0, $10, 0
*/

/* Test case beq:
CLK PC RD1 RD2
program(0x20040000, 0, 0, 0, 0x20050001, 0, 0, 0, 0x10800001, 0, 0, 0, 0x200604d2, 0, 0, 0, 0x20c00000, 0, 0, 0, 0x10a00001, 0, 0, 0, 0x20070001, 0, 0, 0, 0x20070002)
0 0 0 0		# addi $4, $0, 0
C 4 0 0		# addi $5, $0, 1
C 8 0 0		# beq $4, $0, skip
C 16 0 0	# addi $0, $6, 0
C 20 1 0	# beq $5, $0, skip2
C 24 0 0	# addi $7, $0, 1
*/

/* Test case sltiu:
CLK PC RD1 RD2
program(0x200f0007, 0, 0, 0, 0x2010fffd, 0, 0, 0, 0x2df1000d, 0, 0, 0, 0x22200000, 0, 0, 0, 0x2df10003, 0, 0, 0, 0x22200000, 0, 0, 0, 0x2c110000, 0, 0, 0, 0x22200000, 0, 0, 0, 0x2e110000, 0, 0, 0, 0x22200000, 0, 0, 0, 0x2c11fffd, 0, 0, 0, 0x22200000)
0 0 0 0     # addi $15, $0, 7
C 4 0 0     # addi $16, $0, -3
C 8 7 0     # sltiu $17, $15, 13
C 12 1 0    # addi $0, $17, 0
C 16 7 1    # sltiu $17, $15, 3
C 20 0 0    # addi $0, $17, 0
C 24 0 0    # sltiu $17, $0, 0
C 28 0 0    # addi $0, $17, 0
C 32 (-3) 0 # sltiu $17, $16, 0
C 36 0 0    # addi $0, $17, 0
C 40 0 0    # sltiu $17, $0, -3
C 44 1 0    # addi $0, $17, 0
*/

/* Test case sw\_lw:
CLK PC RD1 RD2
program(0x200c000c, 0, 0, 0, 0x200d000d, 0, 0, 0, 0xac0c2000, 0, 0, 0, 0x8c0e2000, 0, 0, 0, 0x21c00000, 0, 0, 0, 0xad8d2000, 0, 0, 0, 0x8d8f2000, 0, 0, 0, 0x21e00000)
0 0 0 0		# addi $12, $0, 12
C 4 0 0		# addi $13, $0, 13
C 8 0 12	# sw $12, 0x2000($0)
C 12 0 0	# lw $14, 0x2000($0)
C 16 12 0	# addi $0, $14, 0
C 20 12 13	# sw $13, 0x2000($12)
C 24 12 0	# lw $15, 0x2000($12)
C 28 13 0	# addi $0, $15, 0
*/

/* Test case and:
CLK PC RD1 RD2
program(0x2008000c, 0, 0, 0, 0x2009000a, 0, 0, 0, 0x01095024, 0, 0, 0, 0x21400000)
0 0 0 0		# addi $8, $0, 12
C 4 0 0		# addi $9, $0, 10
C 8 12 10	# and $10, $8, $9
C 12 8 0	# addi $0, $10, 0
*/

/* Test case slt:
CLK PC RD1 RD2
program(0x200f0007, 0, 0, 0, 0x2010000d, 0, 0, 0, 0x2011fffd, 0, 0, 0, 0x01f0902a, 0, 0, 0, 0x22400000, 0, 0, 0, 0x020f902a, 0, 0, 0, 0x22400000, 0, 0, 0, 0x01ef902a, 0, 0, 0, 0x22400000, 0, 0, 0, 0x022f902a, 0, 0, 0, 0x22400000, 0, 0, 0, 0x01f1902a, 0, 0, 0, 0x22400000)
0 0 0 0     # addi $15, $0, 7
C 4 0 0     # addi $16, $0, 13
C 8 0 0     # addi $17, $0, -3
C 12 7 13   # slt $18, $15, $16
C 16 1 0    # addi $0, $18, 0
C 20 13 7   # slt $18, $16, $15
C 24 0 0    # addi $0, $18, 0
C 28 7 7    # slt $18, $15, $15
C 32 0 0    # addi $0, $18, 0
C 36 (-3) 7 # slt $18, $17, $15
C 40 1 0    # addi $0, $18, 0
C 44 7 (-3) # slt $18, $15, $17
C 48 0 0    # addi $0, $18, 0
*/

/* Test case bne:
CLK PC RD1 RD2
program(0x20040000, 0, 0, 0, 0x20050001, 0, 0, 0, 0x14a00001, 0, 0, 0, 0x200604d2, 0, 0, 0, 0x20c00000, 0, 0, 0, 0x14800001, 0, 0, 0, 0x20070001, 0, 0, 0, 0x20070002)
0 0 0 0		# addi $4, $0, 0
C 4 0 0		# addi $5, $0, 1
C 8 1 0		# bne $5, $0, skip
C 16 0 0	# addi $0, $6, 0
C 20 0 0	# bne $4, $0, skip2
C 24 0 0	# addi $7, $0, 1
*/

/* Test case andi:
CLK PC RD1 RD2
program(0x200b000c, 0, 0, 0, 0x316c000a, 0, 0, 0, 0x21800000)
0 0 0 0		# addi $11, $0, 12
C 4 12 0	# andi $12, $11, 10
C 8 8 0		# addi $0, $12, 0
*/

/* Test case while:
CLK PC RD1 RD2
program(0x20080001, 0, 0, 0, 0x29090005, 0, 0, 0, 0x11200002, 0, 0, 0, 0x21080001, 0, 0, 0, 0x08000001, 0, 0, 0, 0x21000000)
0 0 0 0		# addi $t0, $0, 1
C 4 1 0		# slti $t1, $t0, 5
C 8 1 0		# beq $t1, $0, end
C 12 1 1	# addi $t0, $t0, 1
C 16 x x	# j while
C 4 2 1		# slti $t1, $t0, 5
C 8 1 0		# beq $t1, $0, end
C 12 2 2	# addi $t0, $t0, 1
C 16 x x	# j while
C 4 3 1		# slti $t1, $t0, 5
C 8 1 0		# beq $t1, $0, end
C 12 3 3	# addi $t0, $t0, 1
C 16 x x	# j while
C 4 4 1		# slti $t1, $t0, 5
C 8 1 0		# beq $t1, $0, end
C 12 4 4	# addi $t0, $t0, 1
C 16 x x	# j while
C 4 5 1		# slti $t1, $t0, 5
C 8 0 0		# beq $t1, $0, end
C 20 5 0	# addi $0, $t0, 0
*/
