// Digital circuit priority_encoder.dig as structural Verilog
module priority_encoder (
  input  in0,
  input  in1,
  input  in2,
  input  in3,
  input  in4,
  input  in5,
  input  in6,
  input  in7,
  output [2:0] num,
  output any
);

  PriorityEncoder #(.Selector_Bits(3)) priorityencoder_1 (
    .in0(in0), .in1(in1), .in2(in2), .in3(in3), .in4(in4), .in5(in5), .in6(in6), .in7(in7), .num(num),
    .any(any));
endmodule

/* Test case:
in7 in6 in5 in4 in3 in2 in1 in0 num any
1 x x x x x x x 0b111 1 
0 1 x x x x x x 0b110 1 
0 0 1 x x x x x 0b101 1 
0 0 0 1 x x x x 0b100 1 
0 0 0 0 1 x x x 0b011 1 
0 0 0 0 0 1 x x 0b010 1 
0 0 0 0 0 0 1 x 0b001 1 
0 0 0 0 0 0 0 1 0b000 1 
0 0 0 0 0 0 0 0 0b000 0
*/
